// Logisim project TIc Tac Toe Gane.circ as structural Verilog: 8 circuits, main circuit main
module main (
);

  wire c_1, c_2, c_3, c_4, c_5, c_6, c_7, c_8, c_9, clock_1_out, cpu_1, cpu_2, cpu_3, cpu_4, cpu_5, cpu_6,
       cpu_7, cpu_8, cpu_9, I1, I2, I3, I4, I5, I6, I7, I8, I9, not_1_out, or_1_out, playeroneortwo_1_aout_1,
       playeroneortwo_1_aout_2, playeroneortwo_1_aout_3, playeroneortwo_1_aout_4, playeroneortwo_1_aout_5,
       playeroneortwo_1_aout_6, playeroneortwo_1_aout_7, playeroneortwo_1_aout_8, playeroneortwo_1_aout_9,
       Reset_Score_out, Start_New_Game_out, turn, windetection_1_oplayer, windetection_1_xplayer, withCPU_p2;
  wire [3:0] counter_1_q, counter_2_q;
  wire [5:0] screen_1_out_3, screen_1_out_4, screen_1_out_5, screen_1_out_6, screen_1_out_7, screen_2_out_3,
       screen_2_out_4, screen_2_out_5, screen_2_out_6, screen_2_out_7, writingwinner_1_out_16,
       writingwinner_1_out_17, writingwinner_1_out_18, writingwinner_1_out_19, writingwinner_1_out_20,
       writingwinner_1_out_21, writingwinner_1_out_22, writingwinner_1_out_23, writingwinner_1_out_24,
       writingwinner_1_out_25, writingwinner_1_out_26, writingwinner_1_out_27, writingwinner_1_out_28,
       writingwinner_1_out_29, writingwinner_1_out_30, writingwinner_1_out_31, writingwinner_1_out_32,
       writingwinner_1_out_33, writingwinner_1_out_34, writingwinner_1_out_35, writingwinner_1_out_36,
       writingwinner_1_out_37, writingwinner_1_out_38, writingwinner_1_out_39, writingwinner_1_out_40,
       writingwinner_1_out_41, writingwinner_1_out_42, writingwinner_1_out_43, writingwinner_1_out_44,
       writingwinner_1_out_45, writingwinner_1_out_46, writingwinner_1_out_47, writingwinner_1_out_48,
       writingwinner_1_out_49, writingwinner_1_z1, writingwinner_1_z2, writingwinner_1_z3,
       writingwinner_1_z4, writingwinner_1_z5, writingwinner_1_z6, writingwinner_1_z7, writingwinner_1_z8,
       writingwinner_1_z9, writingwinner_1_z10, writingwinner_1_z11, writingwinner_1_z12,
       writingwinner_1_z13, writingwinner_1_z14;
  wire [29:0] windetection_1_out_12, windetection_1_out_14, windetection_1_out_17, windetection_1_out_19,
       windetection_1_out_21, windetection_1_out_23, windetection_1_out_25, windetection_1_out_27,
       windetection_1_out_30;

  Button button_1 (.out(I1));
  Button button_2 (.out(I4));
  Button button_3 (.out(I7));
  Button button_4 (.out(I2));
  Button button_5 (.out(I5));
  Button button_6 (.out(I8));
  not not_1 (not_1_out, turn);
  Button button_7 (.out(I3));
  Button button_8 (.out(I6));
  Button button_9 (.out(I9));
  Button Start_New_Game (.out(Start_New_Game_out));
  // Switch withCPU: pin names not known; wires that end beside it: 1'b1, withCPU_p2
  DotMatrix #(.matrixrows(6)) dotmatrix_1 (
    .col0(screen_1_out_3), .col1(screen_1_out_4), .col2(screen_1_out_5), .col3(screen_1_out_6),
    .col4(screen_1_out_7));
  Screen screen_1 (
    .O(turn), .X(not_1_out), .out_3(screen_1_out_3), .out_4(screen_1_out_4), .out_5(screen_1_out_5),
    .out_6(screen_1_out_6), .out_7(screen_1_out_7));
  Clock clock_1 (.out(clock_1_out));
  Button Reset_Score (.out(Reset_Score_out));
  Hex_Digit_Display hex_digit_display_1 (.value(counter_1_q));  // open: dp
  Hex_Digit_Display hex_digit_display_2 (.value(counter_2_q));  // open: dp
  Counter #(.max('hf), .width(4)) counter_1 (
    .count(windetection_1_oplayer), .Q(counter_1_q), .clk(windetection_1_oplayer), .clr(Reset_Score_out));  // open: load, D, carry, up
  PlayerOneOrTwo playeroneortwo_1 (
    .l_1(I1), .l_2(I2), .l_3(I3), .l_4(I4), .l_5(I5), .l_6(I6), .l_7(I7), .l_8(I8), .l_9(I9), .player_1(I1),
    .player_2(I2), .player_3(I3), .player_4(I4), .player_5(I5), .player_6(I6), .player_7(I7), .player_8(I8),
    .player_9(I9), .cpu_1(cpu_1), .cpu_2(cpu_2), .cpu_3(cpu_3), .cpu_4(cpu_4), .turn(turn), .cpu_5(cpu_5),
    .cpu_6(cpu_6), .cpu_7(cpu_7), .cpu_8(cpu_8), .cpu_9(cpu_9), .cpuEnable(withCPU_p2),
    .AOut_1(playeroneortwo_1_aout_1), .AOut_2(playeroneortwo_1_aout_2), .AOut_3(playeroneortwo_1_aout_3),
    .AOut_4(playeroneortwo_1_aout_4), .AOut_5(playeroneortwo_1_aout_5), .AOut_6(playeroneortwo_1_aout_6),
    .AOut_7(playeroneortwo_1_aout_7), .AOut_8(playeroneortwo_1_aout_8), .AOut_9(playeroneortwo_1_aout_9));
  GEN gen_1 (
    .c_1(c_1), .c_2(c_2), .c_3(c_3), .c_4(c_4), .c_5(c_5), .c_7(c_7), .c_6(c_6), .c_8(c_8), .c_9(c_9),
    .enable(withCPU_p2), .clk(clock_1_out), .T(turn), .reset(Start_New_Game_out), .cpu_1(cpu_1),
    .cpu_2(cpu_2), .cpu_3(cpu_3), .cpu_4(cpu_4), .cpu_5(cpu_5), .cpu_6(cpu_6), .cpu_7(cpu_7), .cpu_8(cpu_8),
    .cpu_9(cpu_9));
  Counter #(.max('hf), .width(4)) counter_2 (
    .count(windetection_1_xplayer), .Q(counter_2_q), .clk(windetection_1_xplayer), .clr(Reset_Score_out));  // open: load, D, carry, up
  Screen screen_2 (
    .O(windetection_1_oplayer), .X(windetection_1_xplayer), .out_3(screen_2_out_3), .out_4(screen_2_out_4),
    .out_5(screen_2_out_5), .out_6(screen_2_out_6), .out_7(screen_2_out_7));
  windetection windetection_1 (
    .NEXT_GAME(Start_New_Game_out), .A9(playeroneortwo_1_aout_9), .A7(playeroneortwo_1_aout_7),
    .A8(playeroneortwo_1_aout_8), .A1(playeroneortwo_1_aout_1), .A3(playeroneortwo_1_aout_3),
    .A4(playeroneortwo_1_aout_4), .A5(playeroneortwo_1_aout_5), .A6(playeroneortwo_1_aout_6),
    .A2(playeroneortwo_1_aout_2), .out_30(windetection_1_out_30), .out_25(windetection_1_out_25),
    .out_27(windetection_1_out_27), .out_12(windetection_1_out_12), .out_14(windetection_1_out_14),
    .out_23(windetection_1_out_23), .out_19(windetection_1_out_19), .out_21(windetection_1_out_21),
    .out_17(windetection_1_out_17), .Oplayer(windetection_1_oplayer), .Xplayer(windetection_1_xplayer),
    .TURN(turn), .C9(c_9), .C1(c_1), .C8(c_8), .C6(c_6), .C7(c_7), .C2(c_2), .C5(c_5), .C3(c_3), .C4(c_4));
  DotMatrix #(.matrixrows(6)) dotmatrix_2 (
    .col0(screen_2_out_3), .col1(screen_2_out_4), .col2(screen_2_out_5), .col3(screen_2_out_6),
    .col4(screen_2_out_7));
  or or_1 (or_1_out, windetection_1_xplayer, windetection_1_oplayer);
  DotMatrix #(.matrixcols(48), .matrixrows(6)) dotmatrix_3 (
    .col0(writingwinner_1_out_16), .col1(writingwinner_1_z1), .col2(writingwinner_1_out_17),
    .col3(writingwinner_1_out_18), .col4(writingwinner_1_out_19), .col5(writingwinner_1_z2),
    .col6(writingwinner_1_z3), .col7(writingwinner_1_z4), .col8(writingwinner_1_out_20),
    .col9(writingwinner_1_out_21), .col10(writingwinner_1_out_22), .col11(writingwinner_1_z5),
    .col12(writingwinner_1_out_23), .col13(writingwinner_1_out_24), .col14(writingwinner_1_out_25),
    .col15(writingwinner_1_z6), .col16(writingwinner_1_out_26), .col17(writingwinner_1_out_27),
    .col18(writingwinner_1_out_28), .col19(writingwinner_1_z7), .col20(writingwinner_1_z8),
    .col21(writingwinner_1_z9), .col22(writingwinner_1_out_29), .col23(writingwinner_1_out_30),
    .col24(writingwinner_1_out_31), .col25(writingwinner_1_out_32), .col26(writingwinner_1_out_33),
    .col27(writingwinner_1_z10), .col28(writingwinner_1_out_34), .col29(writingwinner_1_z11),
    .col30(writingwinner_1_out_35), .col31(writingwinner_1_out_36), .col32(writingwinner_1_out_37),
    .col33(writingwinner_1_out_38), .col34(writingwinner_1_z12), .col35(writingwinner_1_out_39),
    .col36(writingwinner_1_out_40), .col37(writingwinner_1_out_41), .col38(writingwinner_1_out_42),
    .col39(writingwinner_1_z13), .col40(writingwinner_1_out_43), .col41(writingwinner_1_out_44),
    .col42(writingwinner_1_out_45), .col43(writingwinner_1_z14), .col44(writingwinner_1_out_46),
    .col45(writingwinner_1_out_47), .col46(writingwinner_1_out_48), .col47(writingwinner_1_out_49));
  writingwinner writingwinner_1 (
    .in_1(or_1_out), .out_23(writingwinner_1_out_23), .Z7(writingwinner_1_z7),
    .out_24(writingwinner_1_out_24), .out_25(writingwinner_1_out_25), .Z8(writingwinner_1_z8),
    .out_26(writingwinner_1_out_26), .Z9(writingwinner_1_z9), .out_27(writingwinner_1_out_27),
    .Z10(writingwinner_1_z10), .out_28(writingwinner_1_out_28), .Z11(writingwinner_1_z11),
    .out_29(writingwinner_1_out_29), .Z12(writingwinner_1_z12), .out_30(writingwinner_1_out_30),
    .out_31(writingwinner_1_out_31), .Z13(writingwinner_1_z13), .out_32(writingwinner_1_out_32),
    .Z14(writingwinner_1_z14), .out_33(writingwinner_1_out_33), .out_34(writingwinner_1_out_34),
    .out_35(writingwinner_1_out_35), .out_36(writingwinner_1_out_36), .out_37(writingwinner_1_out_37),
    .out_38(writingwinner_1_out_38), .out_39(writingwinner_1_out_39), .out_40(writingwinner_1_out_40),
    .out_41(writingwinner_1_out_41), .out_16(writingwinner_1_out_16), .out_42(writingwinner_1_out_42),
    .out_43(writingwinner_1_out_43), .out_44(writingwinner_1_out_44), .z1(writingwinner_1_z1),
    .out_45(writingwinner_1_out_45), .out_46(writingwinner_1_out_46), .out_47(writingwinner_1_out_47),
    .out_48(writingwinner_1_out_48), .out_49(writingwinner_1_out_49), .out_17(writingwinner_1_out_17),
    .Z2(writingwinner_1_z2), .out_18(writingwinner_1_out_18), .Z3(writingwinner_1_z3),
    .out_19(writingwinner_1_out_19), .out_20(writingwinner_1_out_20), .Z4(writingwinner_1_z4),
    .out_21(writingwinner_1_out_21), .Z5(writingwinner_1_z5), .out_22(writingwinner_1_out_22),
    .Z6(writingwinner_1_z6));
  DotMatrix #(.matrixrows(6)) dotmatrix_4 (
    .col0(windetection_1_out_12[29:24]), .col1(windetection_1_out_12[23:18]),
    .col2(windetection_1_out_12[17:12]), .col3(windetection_1_out_12[11:6]), .col4(windetection_1_out_12[5:0]));
  DotMatrix #(.matrixrows(6)) dotmatrix_5 (
    .col0(windetection_1_out_19[29:24]), .col1(windetection_1_out_19[23:18]),
    .col2(windetection_1_out_19[17:12]), .col3(windetection_1_out_19[11:6]), .col4(windetection_1_out_19[5:0]));
  DotMatrix #(.matrixrows(6)) dotmatrix_6 (
    .col0(windetection_1_out_25[29:24]), .col1(windetection_1_out_25[23:18]),
    .col2(windetection_1_out_25[17:12]), .col3(windetection_1_out_25[11:6]), .col4(windetection_1_out_25[5:0]));
  DotMatrix #(.matrixrows(6)) dotmatrix_7 (
    .col0(windetection_1_out_14[29:24]), .col1(windetection_1_out_14[23:18]),
    .col2(windetection_1_out_14[17:12]), .col3(windetection_1_out_14[11:6]), .col4(windetection_1_out_14[5:0]));
  DotMatrix #(.matrixrows(6)) dotmatrix_8 (
    .col0(windetection_1_out_21[29:24]), .col1(windetection_1_out_21[23:18]),
    .col2(windetection_1_out_21[17:12]), .col3(windetection_1_out_21[11:6]), .col4(windetection_1_out_21[5:0]));
  DotMatrix #(.matrixrows(6)) dotmatrix_9 (
    .col0(windetection_1_out_27[29:24]), .col1(windetection_1_out_27[23:18]),
    .col2(windetection_1_out_27[17:12]), .col3(windetection_1_out_27[11:6]), .col4(windetection_1_out_27[5:0]));
  DotMatrix #(.matrixrows(6)) dotmatrix_10 (
    .col0(windetection_1_out_17[29:24]), .col1(windetection_1_out_17[23:18]),
    .col2(windetection_1_out_17[17:12]), .col3(windetection_1_out_17[11:6]), .col4(windetection_1_out_17[5:0]));
  DotMatrix #(.matrixrows(6)) dotmatrix_11 (
    .col0(windetection_1_out_23[29:24]), .col1(windetection_1_out_23[23:18]),
    .col2(windetection_1_out_23[17:12]), .col3(windetection_1_out_23[11:6]), .col4(windetection_1_out_23[5:0]));
  DotMatrix #(.matrixrows(6)) dotmatrix_12 (
    .col0(windetection_1_out_30[29:24]), .col1(windetection_1_out_30[23:18]),
    .col2(windetection_1_out_30[17:12]), .col3(windetection_1_out_30[11:6]), .col4(windetection_1_out_30[5:0]));

  // Notes on the sheet:
  //   Player Turn
  //   O PLAYER
  //   X PLAYER
endmodule

module Screen (
  input  O,
  input  X,
  output [5:0] out_3,
  output [5:0] out_4,
  output [5:0] out_5,
  output [5:0] out_6,
  output [5:0] out_7
);

  or or_1 (out_3[5], O, X);

  assign out_3[4:0] = {{4{O}}, out_3[5]};
  assign out_4 = {O, X, 2'b00, X, O};
  assign out_5 = {O, 1'b0, {2{X}}, 1'b0, O};
  assign out_6 = {O, X, 2'b00, X, O};
  assign out_7 = {out_3[5], {4{O}}, out_3[5]};
endmodule

module latchSR (
  input  qd,
  input  qq,
  output QNOT,
  output Q
);

  nor nor_1 (QNOT, qd, Q);
  nor nor_2 (Q, QNOT, qq);
endmodule

module fillBlock (
  input  Val,
  input  enter,
  input  reset,
  output X,
  output BlockCheck,
  output O
);

  wire and_1_out, and_2_out, demultiplexer_1_out0, demultiplexer_1_out1, latchsr_3_qnot, or_1_out;

  Demultiplexer demultiplexer_1 (.out0(demultiplexer_1_out0), .out1(demultiplexer_1_out1), .in(Val), .sel(enter));
  and and_1 (and_1_out, latchsr_3_qnot, demultiplexer_1_out0);
  and and_2 (and_2_out, demultiplexer_1_out1, latchsr_3_qnot);
  latchSR latchsr_1 (.qd(and_1_out), .qq(reset), .Q(X));  // open: QNOT
  latchSR latchsr_2 (.qd(and_2_out), .qq(reset), .Q(O));  // open: QNOT
  or or_1 (or_1_out, X, O);
  latchSR latchsr_3 (.qd(or_1_out), .qq(reset), .QNOT(latchsr_3_qnot), .Q(BlockCheck));
endmodule

module windetection (
  input  A1,
  input  A2,
  input  A3,
  input  A4,
  input  A5,
  input  A6,
  input  A7,
  input  A8,
  input  A9,
  input  NEXT_GAME,
  output C1,
  output [29:0] out_12,
  output C2,
  output [29:0] out_14,
  output Xplayer,
  output C3,
  output [29:0] out_17,
  output C4,
  output [29:0] out_19,
  output C5,
  output [29:0] out_21,
  output C6,
  output [29:0] out_23,
  output C7,
  output [29:0] out_25,
  output C8,
  output [29:0] out_27,
  output Oplayer,
  output C9,
  output [29:0] out_30,
  output TURN
);

  wire and_1_out, and_2_out, and_3_out, and_4_out, and_5_out, and_6_out, and_7_out, and_8_out, and_9_out,
       and_10_out, and_11_out, and_12_out, and_13_out, and_14_out, and_15_out, and_16_out, O00, O01, O02,
       O10, O11, O12, O20, O21, O22, t_ff_1_q, X00, X01, X02, X10, X11, X12, X20, X21, X22;

  T_Flip_Flop t_ff_1 (.T(NEXT_GAME), .clk(1'b1), .Q(t_ff_1_q));  // open: Qn, reset, preset
  // Probe on t_ff_1_q
  fillBlock fillblock_1 (.Val(A1), .enter(TURN), .reset(NEXT_GAME), .X(X00), .BlockCheck(C1), .O(O00));
  fillBlock fillblock_2 (.Val(A2), .enter(TURN), .reset(NEXT_GAME), .X(X01), .BlockCheck(C2), .O(O01));
  fillBlock fillblock_3 (.Val(A3), .enter(TURN), .reset(NEXT_GAME), .X(X02), .BlockCheck(C3), .O(O02));
  fillBlock fillblock_4 (.Val(A4), .enter(TURN), .reset(NEXT_GAME), .X(X10), .BlockCheck(C4), .O(O10));
  fillBlock fillblock_5 (.Val(A5), .enter(TURN), .reset(NEXT_GAME), .X(X11), .BlockCheck(C5), .O(O11));
  fillBlock fillblock_6 (.Val(A6), .enter(TURN), .reset(NEXT_GAME), .X(X12), .BlockCheck(C6), .O(O12));
  fillBlock fillblock_7 (.Val(A7), .enter(TURN), .reset(NEXT_GAME), .X(X20), .BlockCheck(C7), .O(O20));
  fillBlock fillblock_8 (.Val(A8), .enter(TURN), .reset(NEXT_GAME), .X(X21), .BlockCheck(C8), .O(O21));
  fillBlock fillblock_9 (.Val(A9), .enter(TURN), .reset(NEXT_GAME), .X(X22), .BlockCheck(C9), .O(O22));
  xor xor_1 (TURN, t_ff_1_q, C1, C2, C3, C4, C5, C6, C7, C8, C9);
  Screen screen_1 (
    .O(O00), .X(X00), .out_3(out_12[5:0]), .out_4(out_12[11:6]), .out_5(out_12[17:12]),
    .out_6(out_12[23:18]), .out_7(out_12[29:24]));
  Screen screen_2 (
    .O(O20), .X(X20), .out_3(out_25[5:0]), .out_4(out_25[11:6]), .out_5(out_25[17:12]),
    .out_6(out_25[23:18]), .out_7(out_25[29:24]));
  Screen screen_3 (
    .O(O22), .X(X22), .out_3(out_30[5:0]), .out_4(out_30[11:6]), .out_5(out_30[17:12]),
    .out_6(out_30[23:18]), .out_7(out_30[29:24]));
  Screen screen_4 (
    .O(O01), .X(X01), .out_3(out_14[5:0]), .out_4(out_14[11:6]), .out_5(out_14[17:12]),
    .out_6(out_14[23:18]), .out_7(out_14[29:24]));
  Screen screen_5 (
    .O(O02), .X(X02), .out_3(out_17[5:0]), .out_4(out_17[11:6]), .out_5(out_17[17:12]),
    .out_6(out_17[23:18]), .out_7(out_17[29:24]));
  Screen screen_6 (
    .O(O10), .X(X10), .out_3(out_19[5:0]), .out_4(out_19[11:6]), .out_5(out_19[17:12]),
    .out_6(out_19[23:18]), .out_7(out_19[29:24]));
  Screen screen_7 (
    .O(O11), .X(X11), .out_3(out_21[5:0]), .out_4(out_21[11:6]), .out_5(out_21[17:12]),
    .out_6(out_21[23:18]), .out_7(out_21[29:24]));
  Screen screen_8 (
    .O(O12), .X(X12), .out_3(out_23[5:0]), .out_4(out_23[11:6]), .out_5(out_23[17:12]),
    .out_6(out_23[23:18]), .out_7(out_23[29:24]));
  Screen screen_9 (
    .O(O21), .X(X21), .out_3(out_27[5:0]), .out_4(out_27[11:6]), .out_5(out_27[17:12]),
    .out_6(out_27[23:18]), .out_7(out_27[29:24]));
  and and_1 (and_1_out, X00, X10, X20);
  and and_2 (and_2_out, O00, O10, O20);
  and and_3 (and_3_out, X20, X21, X22);
  and and_4 (and_4_out, O20, O21, O22);
  and and_5 (and_5_out, X00, X11, X22);
  and and_6 (and_6_out, X01, X11, X21);
  and and_7 (and_7_out, O00, O01, O02);
  and and_8 (and_8_out, O00, O11, O22);
  and and_9 (and_9_out, O01, O11, O21);
  and and_10 (and_10_out, X00, X01, X02);
  and and_11 (and_11_out, O02, O12, O22);
  and and_12 (and_12_out, X10, X11, X12);
  and and_13 (and_13_out, X02, X12, X22);
  and and_14 (and_14_out, O10, O11, O12);
  and and_15 (and_15_out, O02, O11, O20);
  and and_16 (and_16_out, X02, X11, X20);
  or or_1 (Xplayer, and_10_out, and_1_out, and_5_out, and_12_out, and_16_out, and_3_out, and_6_out, and_13_out);
  or or_2 (Oplayer, and_7_out, and_2_out, and_8_out, and_14_out, and_15_out, and_4_out, and_9_out, and_11_out);

  // Other names for the same wires on the sheet: B1 = C1; B2 = C2; B3 = C3; B4 = C4; B5 = C5; B6 = C6; B7 = C7;
  //   B8 = C8; B9 = C9
endmodule

module writingwinner (
  input  in_1,
  output [5:0] z1,
  output [5:0] Z2,
  output [5:0] Z3,
  output [5:0] Z4,
  output [5:0] Z5,
  output [5:0] Z6,
  output [5:0] Z7,
  output [5:0] Z8,
  output [5:0] Z9,
  output [5:0] Z10,
  output [5:0] Z11,
  output [5:0] Z12,
  output [5:0] Z13,
  output [5:0] Z14,
  output [5:0] out_16,
  output [5:0] out_17,
  output [5:0] out_18,
  output [5:0] out_19,
  output [5:0] out_20,
  output [5:0] out_21,
  output [5:0] out_22,
  output [5:0] out_23,
  output [5:0] out_24,
  output [5:0] out_25,
  output [5:0] out_26,
  output [5:0] out_27,
  output [5:0] out_28,
  output [5:0] out_29,
  output [5:0] out_30,
  output [5:0] out_31,
  output [5:0] out_32,
  output [5:0] out_33,
  output [5:0] out_34,
  output [5:0] out_35,
  output [5:0] out_36,
  output [5:0] out_37,
  output [5:0] out_38,
  output [5:0] out_39,
  output [5:0] out_40,
  output [5:0] out_41,
  output [5:0] out_42,
  output [5:0] out_43,
  output [5:0] out_44,
  output [5:0] out_45,
  output [5:0] out_46,
  output [5:0] out_47,
  output [5:0] out_48,
  output [5:0] out_49
);


  assign out_16 = {2'b00, in_1, 1'b0, {2{in_1}}};
  assign out_17 = {3'b000, in_1, 1'b0, in_1};
  assign out_18 = {2'b00, {2{in_1}}, 1'b0, in_1};
  assign out_19 = {2'b00, in_1, 1'b0, in_1, 1'b0};
  assign out_20 = {6{in_1}};
  assign out_21 = {2'b00, in_1, 3'b000};
  assign out_22 = {2'b00, in_1, 3'b000};
  assign out_23 = {1'b0, {5{in_1}}};
  assign out_24 = {3'b000, in_1, 2'b00};
  assign out_25 = {3'b000, {3{in_1}}};
  assign out_26 = {2'b00, {4{in_1}}};
  assign out_27 = {2'b00, {2{in_1}}, 1'b0, in_1};
  assign out_28 = {2'b00, {2{in_1}}, 1'b0, in_1};
  assign out_29 = {2'b00, {3{in_1}}, 1'b0};
  assign out_30 = {{5{1'b0}}, in_1};
  assign out_31 = {3'b000, {2{in_1}}, 1'b0};
  assign out_32 = {{5{1'b0}}, in_1};
  assign out_33 = {2'b00, {3{in_1}}, 1'b0};
  assign out_34 = {2'b00, in_1, 1'b0, {2{in_1}}};
  assign out_35 = {2'b00, {4{in_1}}};
  assign out_36 = {3'b000, in_1, 2'b00};
  assign out_37 = {3'b000, in_1, 2'b00};
  assign out_38 = {4'b0000, {2{in_1}}};
  assign out_39 = {2'b00, {4{in_1}}};
  assign out_40 = {3'b000, in_1, 2'b00};
  assign out_41 = {3'b000, in_1, 2'b00};
  assign out_42 = {4'b0000, {2{in_1}}};
  assign out_43 = {2'b00, {4{in_1}}};
  assign out_44 = {2'b00, {2{in_1}}, 1'b0, in_1};
  assign out_45 = {2'b00, {2{in_1}}, 1'b0, in_1};
  assign out_46 = {2'b00, {4{in_1}}};
  assign out_47 = {3'b000, in_1, 2'b00};
  assign out_48 = {3'b000, in_1, 2'b00};
  assign out_49 = {2'b00, in_1, 3'b000};
  assign z1 = {6{1'b0}};
  assign Z2 = {6{1'b0}};
  assign Z3 = {6{1'b0}};
  assign Z4 = {6{1'b0}};
  assign Z5 = {6{1'b0}};
  assign Z6 = {6{1'b0}};
  assign Z7 = {6{1'b0}};
  assign Z8 = {6{1'b0}};
  assign Z9 = {6{1'b0}};
  assign Z10 = {6{1'b0}};
  assign Z11 = {6{1'b0}};
  assign Z12 = {6{1'b0}};
  assign Z13 = {6{1'b0}};
  assign Z14 = {6{1'b0}};
endmodule

module GEN (
  input  c_1,
  input  c_2,
  input  c_3,
  input  c_4,
  input  c_5,
  input  c_7,
  input  c_6,
  input  c_8,
  input  c_9,
  input  enable,
  input  clk,
  input  T,
  input  reset,
  output cpu_1,
  output cpu_2,
  output cpu_3,
  output cpu_4,
  output cpu_5,
  output cpu_6,
  output cpu_7,
  output cpu_8,
  output cpu_9
);

  wire and_2_out, comparator_1_eq, demultiplexer_1_out9, multiplexer_1_out, not_1_out, random_1_p2;
  wire [3:0] undriven;

  // Random #(.seed(10), .trigger("falling"), .width(4)) random_1: pin names not known; wires that end beside it: enable, random_1_p2, reset
  and and_1 (random_1_p2, T, not_1_out);
  Multiplexer #(.select(4)) multiplexer_1 (
    .in0(c_1), .in1(c_2), .in2(c_3), .in3(c_4), .in4(c_5), .in5(c_6), .in6(c_7), .in7(c_8), .in8(c_9),
    .in9(1'b1), .in10(1'b1), .in11(1'b1), .in12(1'b1), .in13(1'b1), .in14(1'b1), .in15(1'b1),
    .out(multiplexer_1_out), .sel(undriven));
  Demultiplexer #(.select(4)) demultiplexer_1 (
    .out0(cpu_1), .out1(cpu_2), .out2(cpu_3), .out3(cpu_4), .out4(cpu_5), .out5(cpu_6), .out6(cpu_7),
    .out7(cpu_8), .out8(cpu_9), .out9(demultiplexer_1_out9), .out10(demultiplexer_1_out9),
    .out11(demultiplexer_1_out9), .out12(demultiplexer_1_out9), .out13(demultiplexer_1_out9),
    .out14(demultiplexer_1_out9), .out15(demultiplexer_1_out9), .in(1'b1), .sel(undriven));
  Comparator #(.width(1)) comparator_1 (.a(multiplexer_1_out), .b(1'b1), .eq(comparator_1_eq));  // open: gt, lt
  and and_2 (and_2_out, clk, comparator_1_eq);
  not not_1 (not_1_out, and_2_out);
  // also tied to GND on the sheet: demultiplexer_1_out9
endmodule

module PlayerOneOrTwo (
  input  l_1,
  input  l_2,
  input  l_3,
  input  l_4,
  input  l_5,
  input  l_6,
  input  l_7,
  input  l_8,
  input  l_9,
  input  player_1,
  input  player_2,
  input  player_3,
  input  player_4,
  input  player_5,
  input  player_6,
  input  player_7,
  input  player_8,
  input  player_9,
  input  cpu_1,
  input  cpu_2,
  input  cpu_3,
  input  cpu_4,
  input  turn,
  input  cpu_5,
  input  cpu_6,
  input  cpu_7,
  input  cpu_8,
  input  cpu_9,
  input  cpuEnable,
  output AOut_1,
  output AOut_2,
  output AOut_3,
  output AOut_4,
  output AOut_5,
  output AOut_6,
  output AOut_7,
  output AOut_8,
  output AOut_9
);

  wire and_1_out, and_2_out, and_3_out, and_4_out, and_5_out, and_6_out, and_7_out, and_8_out, and_9_out,
       and_10_out, and_11_out, and_12_out, and_13_out, and_14_out, and_15_out, and_16_out, and_17_out,
       and_18_out, and_19_out, and_20_out, and_21_out, and_22_out, and_23_out, and_24_out, and_25_out,
       and_26_out, and_27_out, and_28_out, and_29_out, and_30_out, and_31_out, and_32_out, and_33_out,
       and_34_out, and_35_out, and_36_out, not_1_out, not_2_out, playSecond_1, playSecond_2, playSecond_3,
       playSecond_4, playSecond_5, playSecond_6, playSecond_7, playSecond_8, playSecond_9;

  and and_1 (and_1_out, not_1_out, player_1);
  and and_2 (and_2_out, not_1_out, player_2);
  and and_3 (and_3_out, not_1_out, player_3);
  and and_4 (and_4_out, not_1_out, player_4);
  and and_5 (and_5_out, not_1_out, player_5);
  and and_6 (and_6_out, not_1_out, player_6);
  and and_7 (and_7_out, not_1_out, player_7);
  and and_8 (and_8_out, not_1_out, player_8);
  and and_9 (and_9_out, not_1_out, player_9);
  not not_1 (not_1_out, cpuEnable);
  and and_10 (and_10_out, cpuEnable, cpu_1);
  and and_11 (and_11_out, cpuEnable, cpu_2);
  and and_12 (and_12_out, cpuEnable, cpu_3);
  and and_13 (and_13_out, cpuEnable, cpu_4);
  and and_14 (and_14_out, cpuEnable, cpu_5);
  and and_15 (and_15_out, cpuEnable, cpu_6);
  and and_16 (and_16_out, cpuEnable, cpu_7);
  and and_17 (and_17_out, cpuEnable, cpu_8);
  and and_18 (and_18_out, cpuEnable, cpu_9);
  or or_1 (playSecond_1, and_10_out, and_1_out);
  or or_2 (playSecond_2, and_11_out, and_2_out);
  or or_3 (playSecond_3, and_12_out, and_3_out);
  or or_4 (playSecond_4, and_13_out, and_4_out);
  or or_5 (playSecond_5, and_14_out, and_5_out);
  or or_6 (playSecond_6, and_15_out, and_6_out);
  or or_7 (playSecond_7, and_16_out, and_7_out);
  or or_8 (playSecond_8, and_17_out, and_8_out);
  or or_9 (playSecond_9, and_18_out, and_9_out);
  and and_19 (and_19_out, l_1, not_2_out);
  and and_20 (and_20_out, l_2, not_2_out);
  and and_21 (and_21_out, l_3, not_2_out);
  and and_22 (and_22_out, l_4, not_2_out);
  and and_23 (and_23_out, l_5, not_2_out);
  and and_24 (and_24_out, l_6, not_2_out);
  and and_25 (and_25_out, l_7, not_2_out);
  and and_26 (and_26_out, l_8, not_2_out);
  and and_27 (and_27_out, l_9, not_2_out);
  not not_2 (not_2_out, turn);
  and and_28 (and_28_out, playSecond_1, turn);
  and and_29 (and_29_out, playSecond_2, turn);
  and and_30 (and_30_out, playSecond_3, turn);
  and and_31 (and_31_out, playSecond_4, turn);
  and and_32 (and_32_out, playSecond_5, turn);
  and and_33 (and_33_out, playSecond_6, turn);
  and and_34 (and_34_out, playSecond_7, turn);
  and and_35 (and_35_out, playSecond_8, turn);
  and and_36 (and_36_out, playSecond_9, turn);
  or or_10 (AOut_1, and_19_out, and_28_out);
  or or_11 (AOut_2, and_20_out, and_29_out);
  or or_12 (AOut_3, and_21_out, and_30_out);
  or or_13 (AOut_4, and_22_out, and_31_out);
  or or_14 (AOut_5, and_23_out, and_32_out);
  or or_15 (AOut_6, and_24_out, and_33_out);
  or or_16 (AOut_7, and_25_out, and_34_out);
  or or_17 (AOut_8, and_26_out, and_35_out);
  or or_18 (AOut_9, and_27_out, and_36_out);
endmodule
